// Logisim project MIPS.circ as structural Verilog: 1 circuit, main circuit main
module main (
  output [11:0] out_1,
  output [19:0] out_2
);

  wire alu_1_p4, and_1_out, and_2_out, multiplexer_3_out, not_1_out, register_file_1_p7;
  wire [3:0] multiplexer_1_out;
  wire [7:0] adder_1_out, adder_2_out, alu_1_p5, multiplexer_2_out, multiplexer_4_out, multiplexer_6_out,
       ram_1_data, register_1_q, register_file_1_p1, register_file_1_p8;

  Register register_1 (.D(multiplexer_6_out), .Q(register_1_q));  // open: en, clk, clr
  Adder adder_1 (.a(8'h1), .b(register_1_q), .out(adder_1_out));  // open: cin, cout
  ROM #(.dataWidth(20)) rom_1 (.addr(register_1_q), .data(out_2));  // open: sel
  Multiplexer #(.width(4), .enable("false")) multiplexer_1 (
    .in0(out_2[11:8]), .in1(out_2[7:4]), .out(multiplexer_1_out), .sel(out_1[10]));
  ROM #(.addrWidth(4), .dataWidth(12)) rom_2 (.addr(out_2[19:16]), .data(out_1));  // open: sel
  // Register_File register_file_1: pin names not known; wires that end beside it: register_file_1_p1, out_2[15:12], out_2[11:8], multiplexer_1_out, multiplexer_1_out, out_1[8], register_file_1_p7, register_file_1_p8
  Multiplexer #(.width(8), .enable("false")) multiplexer_2 (
    .in0(register_file_1_p8), .in1(out_2[7:0]), .out(multiplexer_2_out), .sel(out_1[9]));
  // ALU alu_1: pin names not known; wires that end beside it: register_file_1_p7, multiplexer_2_out, out_1[2:0], alu_1_p4, alu_1_p5
  Adder adder_2 (.a(adder_1_out), .b(out_2[7:0]), .out(adder_2_out));  // open: cin, cout
  Multiplexer #(.enable("false")) multiplexer_3 (
    .in0(and_1_out), .in1(and_2_out), .out(multiplexer_3_out), .sel(out_1[4]));
  and and_1 (and_1_out, out_1[5], alu_1_p4);
  RAM #(.bus("separate")) ram_1 (
    .addr(alu_1_p5), .data(ram_1_data), .str(out_1[6]), .ld(out_1[7]));  // open: din, sel, clk, clr
  Multiplexer #(.width(8), .enable("false")) multiplexer_4 (
    .in0(adder_1_out), .in1(adder_2_out), .out(multiplexer_4_out), .sel(multiplexer_3_out));
  and and_2 (and_2_out, out_1[5], not_1_out);
  not not_1 (not_1_out, alu_1_p4);
  Multiplexer #(.width(8), .enable("false")) multiplexer_5 (
    .in0(ram_1_data), .in1(alu_1_p5), .out(register_file_1_p1), .sel(out_1[10]));
  Multiplexer #(.width(8), .enable("false")) multiplexer_6 (
    .in0(multiplexer_4_out), .in1(out_2[7:0]), .out(multiplexer_6_out), .sel(out_1[3]));

  // Notes on the sheet:
  //   contents of rom_1 (hex, n*v repeats v):
  //   43420 d3510 62150 f3420 54420 32a e0542 832fc 732f6 b32f6 332f6 932fc a530a 97200 87701 76203 97600
  //   87701 a7300 77701 23200 114f0 c0000 c0700 c1600
  //   RegWrite
  //   contents of rom_2 (hex, n*v repeats v):
  //   245 9 9 42 240 244 243 40 41 110 1e0 43 7 241 246 242
  //   RegDst
  //   ALUOp
  //   ALUSrc
  //   Jump
  //   Beqone
  //   Branch
  //   RegDst
  //   MemWrite
  //   MemRead
endmodule
